# Fritzing sketch sonar (saved by Fritzing 0.9.3b)

parts:
  X2 = Sonar
  Componente1 = Arduino Uno (Rev3)

nets:
  N1: X2.+5, Componente1.5V
  N2: X2.SDA, Componente1.GND
  N3: X2.SCL, Componente1.D5_PWM
  N4: X2.n/c, Componente1.D4

custom parts:
  Sonar: Devantech SRF08 sonar range-finder. I2C interface. Other Devantech sonars similar
